# Fritzing sketch Robot_Bluetooch_Car (saved by Fritzing 0.9.3b)
circuit board: 8.46667cm x 5.64444cm

parts:
  Часть1 = Arduino Uno (Rev3)
  Часть2 = Motor Driver 1A Dual TB6612FNG
  Часть3 = Bluetooth HC-05 Macho
  M1 = DC Motor
  M2 = DC Motor
  C1 = Ceramic Capacitor [capacitance=100nF voltage=16V package="100 mil [THT, multilayer]"]
  C2 = Ceramic Capacitor [capacitance=100nF voltage=16V package="100 mil [THT, multilayer]"]

nets:
  N1: Часть1.D8, Часть2.BIN1
  N2: Часть1.D9_PWM, Часть2.BIN2
  N3: Часть1.D10_PWM/SS, Часть2.PWMB
  N4: Часть1.D2, Часть3.TXD
  N5: Часть1.D3_PWM, Часть3.RXD
  N6: Часть1.D4, Часть2.PWMA
  N7: Часть1.D5_PWM, Часть2.AIN2
  N8: Часть1.D6_PWM, Часть2.AIN1
  5V: Часть1.5V, Часть3.VCC
  GND: Часть1.GND, Часть3.GND
  N9: Часть2.B01, M1.pin_1, C1.1
  N10: Часть2.B02, M1.pin_2, C1.0
  N11: Часть2.A02, M2.pin_1, C2.1
  N12: Часть2.A01, M2.pin_2, C2.0
  N13: Часть2.VCC, Часть2.STBY
